# Fritzing sketch mega-cerrojo-v1 (saved by Fritzing 0.9.6b)
breadboards: 1

parts:
  Matrix_keypad1 = KEYPAD 4x4
  Componente1 = Arduino Mega 2560 (Rev3)
  LED1 = RGB LED (com. cathode, rgb) [package="5 mm [THT]"]
  R1 = Resistor [tolerance=±5% resistance=220 package="0402 [SMD]"]
  R2 = Resistor [tolerance=±5% resistance=220 package="0402 [SMD]"]
  R3 = Resistor [tolerance=±5% resistance=220 package="0402 [SMD]"]
  MH-ET_LIVE_ESP32_DEVKIT1 = MH-ET LIVE ESP32 DEVKIT 38 pins
  J1 = Basic Servo

nets:
  N1: Matrix_keypad1.col1, Componente1.D30
  N2: Matrix_keypad1.col2, Componente1.D32
  N3: Matrix_keypad1.col3, Componente1.D34
  N4: Matrix_keypad1.col4, Componente1.D36
  N5: Matrix_keypad1.row1, Componente1.D22
  N6: Matrix_keypad1.row2, Componente1.D24
  N7: Matrix_keypad1.row3, Componente1.D26
  N8: Matrix_keypad1.row4, Componente1.D28
  N9: Componente1.D17_PWM/RX2, MH-ET_LIVE_ESP32_DEVKIT1.IO16
  N10: Componente1.D16_PWM/TX2, MH-ET_LIVE_ESP32_DEVKIT1.IO17
  N11: Componente1.GND, LED1.common_cathode
  N12: Componente1.D9_PWM, J1.pulse
  N13: Componente1.D44, R2.Pin_0
  N14: Componente1.D45, R1.Pin_0
  N15: Componente1.D46, R3.Pin_0
  N16: LED1.red_anode, R2.Pin_1
  N17: LED1.green_anode, R1.Pin_1
  N18: LED1.blue_anode, R3.Pin_1
  N19: MH-ET_LIVE_ESP32_DEVKIT1.GND#64, J1.gnd

custom parts:
  KEYPAD 4x4: Matrix keypad 16 buttons, 4 rows x 4 columns
  MH-ET LIVE ESP32 DEVKIT 38 pins: http://mh.nodebb.com/topic/2/mh-et-live-esp32-devkit

// code stored in the sketch: mega-cerrojo-v1.fzz.ino

